# Fritzing sketch notgate (saved by Fritzing 0.7.9b)
breadboards: 1

parts:
  Arduino1 = Arduino
  part = PICAXE-28A [package=THT]  # not connected
  part_2 = SN74LS14N [package="DIP14 [THT]"]  # not connected
  part_3 = Hex Inverter Schmitt Trigger SN74HC14 [package="DIP (Dual Inline)"]  # not connected
  U1 = SN74LS14N [package="DIP14 [THT]"]
  S1 = Pushbutton [package=THT]
  R1 = Resistor [tolerance=±5% resistance=10k package=THT]

nets:
  N1: Arduino1.D12, U1.6A, S1.leg0, R1.Pin_0
  N2: Arduino1.D11, U1.6Y
  +5V: Arduino1.+5V, U1.VCC, S1.leg1
  GND: Arduino1.GND, U1.GND, R1.Pin_1
